# Fritzing sketch ph-metre_uno (saved by Fritzing 0.9.3b)
circuit board: 6.9215cm x 5.33756cm
breadboards: 1

parts:
  Sonde_PH = male pin header, 3 pins [form="♂ (male)"]
  Composant1 = Arduino Prototyping Shield
  PCB1 = Arduino Shield PCB  # not connected
  PT-100 = Adafruit MAX31865 RTD Sensor Breakout [part_number="Adafruit #3328"]

nets:
  GND: Sonde_PH.pin1, Composant1.GND, PT-100.GND
  N1: Sonde_PH.pin2, Composant1.+5V
  N2: Sonde_PH.pin3, Composant1.A0
  N3: Composant1.D10, PT-100.CS
  N4: Composant1.D11, PT-100.SDI
  N5: Composant1.D12, PT-100.SDO
  N6: Composant1.D13, PT-100.SCLK
  3.3V: Composant1.3.3V, PT-100.3.3V

custom parts:
  Arduino Shield PCB: Plain PCB Shaped to fit an Arduino "Shield"
  Adafruit MAX31865 RTD Sensor Breakout: For precision temperature sensing, nothing beats a Platinum RTD. Resistance temperature detectors (RTDs) are temperature sensors that contain a resistor that changes resistance value as its temperature changes, basically a kind of thermistor. In this sensor, the resistor is actually a small strip of Platinum with a resistance of 100 ohms at 0°C, thus the name PT100. Compared to most NTC/PTC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
